# Fritzing sketch conexiones (saved by Fritzing 0.9.3b)
breadboards: 1

parts:
  Part3 = Arduino Nano (Rev3.0)
  DS1 = DS18B20 1-Wire Temperature Sensor [part_number=DS18B20]
  Grove1 = Grove OLED 128x96
  JP2 = Header 6 [package=molex-1x6_lock]
  RE1 = Rotary Encoder [package=THT]
  R2 = Resistor [tolerance=±5% resistance=10k package=THT]

nets:
  GND: Part3.GND, DS1.GND, Grove1.GND, JP2.6
  N1: Part3.D2, RE1.EncoderPinB
  N2: Part3.D3, RE1.EncoderPinA
  N3: Part3.D5, JP2.3
  N4: Part3.D6, DS1.DQ, R2.Pin_0
  N5: Part3.D7, Grove1.SDA
  N6: Part3.D8, Grove1.SCL
  5V: Part3.5V, Grove1.VCC, RE1.EncoderPinC
  N7: Part3.A1, JP2.2
  3V3: Part3.3V3, DS1.VDD, R2.Pin_1
